# Fritzing sketch complete-circuit (saved by Fritzing 0.9.3b)

parts:
  Part1 = Arduino Nano (Rev3.0) (ICSP)
  Part2 = InvenSense MPU6050
  microSD1 = MicroSD Card Module
  U1 = SWITCH_SPDT [package=kps-1290]
  LED1 = smd LED [color="Red (633nm)" package="0805 [SMD]"]
  R1 = Resistor [tolerance=±5% resistance=220 package="0603 [SMD]"]

nets:
  GND: Part1.GND, Part2.GND, microSD1.GND, U1.P, LED1.cathode
  N1: Part1.D2, Part2.INT
  N2: Part1.D7, U1.O
  N3: Part1.D8, R1.Pin_1
  N4: Part1.D10, microSD1.CS
  N5: Part1.D11/MOSI, microSD1.MOSI
  N6: Part1.D12/MISO, microSD1.MISO
  VCC: Part1.5V, Part2.VCC, microSD1.VCC
  N7: Part1.A5, Part2.SCL
  N8: Part1.A4, Part2.SDA
  N9: Part1.D13/SCK, microSD1.SCK
  N10: LED1.anode, R1.Pin_0
